// Logisim project OurProject.circ as structural Verilog: 11 circuits, main circuit main
module I_O_mapped (
  input  [15:0] add,
  input  data,
  input  clock,
  input  rd_wr,
  input  [7:0] I_Odata,
  output [5:0] out_6,
  output out_7,
  output out_8,
  output out_9,
  output [7:0] out_10
);

  wire nor_1_out;

  nor nor_1 (nor_1_out, add[10], add[6], add[7], add[8], add[9], add[11], add[12], add[13], add[14], add[15]);
  and and_1 (out_7, ~nor_1_out, data);  // AND_Gate
  and and_2 (out_8, data, clock, nor_1_out);

  assign out_6 = add[5:0];
  assign out_9 = rd_wr;
  assign out_10 = I_Odata;
endmodule

module main (
);

  wire cdm_8_mark5_1_p1, cdm_8_mark5_1_p2, cdm_8_mark5_1_p4, cdm_8_mark5_1_p5, cdm_8_mark5_1_p6,
       cdm_8_mark5_1_p7, cdm_8_mark5_1_p8, cdm_8_mark5_1_p9, CL, code, data, I_Osel, IN_OUT, mem, not_1_out,
       RAM, rd_wr;
  wire [1:0] joystick_in;
  wire [5:0] I_Oaddr;
  wire [7:0] cdm_8_mark5_1_p13, cdm_8_mark5_1_p14, data_out, I_Odata, score_left, score_right;
  wire [15:0] cdm_8_mark5_1_p12;

  Clock clock_1 (.out(CL));
  // Probe on cdm_8_mark5_1_p5
  // Probe on cdm_8_mark5_1_p2
  // Probe on cdm_8_mark5_1_p4
  // Probe on cdm_8_mark5_1_p1
  // Probe on cdm_8_mark5_1_p6
  // Probe on cdm_8_mark5_1_p7
  // Probe on cdm_8_mark5_1_p8
  // CdM_8_mark5 cdm_8_mark5_1: pin names not known; wires that end beside it: cdm_8_mark5_1_p1, cdm_8_mark5_1_p2, CL, cdm_8_mark5_1_p4, cdm_8_mark5_1_p5, cdm_8_mark5_1_p6, cdm_8_mark5_1_p7, cdm_8_mark5_1_p8, cdm_8_mark5_1_p9, mem, rd_wr, cdm_8_mark5_1_p12, cdm_8_mark5_1_p13, cdm_8_mark5_1_p14
  assign data_out = not_1_out ? cdm_8_mark5_1_p13 : 8'bz;  // Controlled_Buffer controlled_buffer_1
  not not_1 (not_1_out, rd_wr);
  assign cdm_8_mark5_1_p14 = rd_wr ? data_out : 8'bz;  // Controlled_Buffer controlled_buffer_2
  Decoder #(.disabled(0)) decoder_1 (.out0(code), .out1(data), .sel(cdm_8_mark5_1_p9), .en(mem));
  I_O_mapped i_o_mapped_1 (
    .add(cdm_8_mark5_1_p12), .data(data), .clock(CL), .rd_wr(rd_wr), .I_Odata(data_out), .out_6(I_Oaddr),
    .out_7(RAM), .out_8(I_Osel), .out_9(IN_OUT), .out_10(I_Odata));
  score_right score_right_1 (
    .I_Osel(I_Osel), .IN_OUT(IN_OUT), .Cl(CL), .I_Oaddr(I_Oaddr), .data(I_Odata), .value(score_right),
    .data_out(data_out));
  score_left score_left_1 (
    .I_Osel(I_Osel), .IN_OUT(IN_OUT), .Cl(CL), .I_Oaddr(I_Oaddr), .data(I_Odata), .value(score_left),
    .data_out(data_out));
  Update update_1 (.I_Osel(I_Osel), .IN_OUT(IN_OUT), .Cl(CL), .I_Oaddr(I_Oaddr), .data(I_Odata), .data_out(data_out));
  Random random_1 (.I_Osel(I_Osel), .IN_OUT(IN_OUT), .Cl(CL), .I_Oaddr(I_Oaddr), .data_out(data_out));
  ROM #(.addrWidth(16)) rom_1 (.addr(cdm_8_mark5_1_p12), .data(data_out), .sel(code));
  RAM #(.addrWidth(16)) ram_1 (
    .addr(cdm_8_mark5_1_p12), .data(data_out), .sel(RAM), .clk(CL), .ld(rd_wr));  // open: clr
  TV_TENNIS tv_tennis_1 (
    .Cl(CL), .I_Osel(I_Osel), .I_Odata(I_Odata), .IN_OUT(IN_OUT), .score_left(score_left),
    .score_right(score_right), .I_Oaddr(I_Oaddr), .data_out(data_out), .Joystick(joystick_in));
  Joystick joystick_1 (
    .I_Osel(I_Osel), .IN_OUT(IN_OUT), .Cl(CL), .I_Oaddr(I_Oaddr), .Joystik_in(joystick_in),
    .data_out(data_out));

  // Notes on the sheet:
  //   contents of rom_1 (hex, n*v repeats v):
  //   66*0 3f 5e 4*0 d1 21 d2 0 a6 d1 22 a6 d1 24 d2 f a6 d1 25 d2 f a6 d0 23 d1 29 b5 a1 d0 0 d1 6e 8c a1
  //   d0 1f d1 6e 88 a1 d0 0 0 e1 1f d0 0 ac d6 2b 1 d6 b8 0 d0 26 b3 d0 0 13 d2 25 ba d1 20 59 ad d6 90 0
  //   d6 a6 0 ee de d4 d0 1e b0 8c d1 1f 41 d2 25 ba 79 e2 6 d6 63 1 ee 4 d6 58 1 d7 d0 20 b0 0 e1 6 d6 42
  //   1 ee 7 0 e4 4 d6 4d 1 d7 d0 24 b0 d1 1e 71 eb 32 d0 25 b0 d1 1e b5 d2 1f 46 8e 72 e0 a 8e 72 e0 6 8a
  //   8a 72 e1 c d1 27 a4 d0 26 b3 d0 26 b3 ee 11 d0 21 b1 8d d0 21 a1 d0 e 71 e2 2 d4 dd 50 0 d0 24 b0 d1
  //   1 74 eb 32 d0 25 b0 d1 1 b5 8d d2 1f 46 72 e0 a 8e 72 e0 6 8a 8a 72 e1 c d1 27 a4 d0 26 b3 d0 26 b3
  //   ee 11 d0 22 b1 8d d0 22 a1 d0 e 71 e2 2 d4 dd 50 0 d7 d0 25 b0 d1 1f 71 eb 4 d1 28 a4 d0 25 b0 d1 0
  //   74 eb 4 d1 28 a4 d7 d0 1 b1 d2 7d 76 e0 3 8d a1 d7 d0 1 b1 d2 60 79 e0 3 89 a1 d7 d0 1e b1 d2 7d 76
  //   e0 3 8d a1 d7 d0 1e b1 d2 60 79 e0 3 89 a1 d7
endmodule

module video_buffer (
  input  [5:0] video_addr,
  input  sel,
  input  in_out,
  input  clock,
  input  [7:0] data,
  output [31:0] out_6,
  output [31:0] out_7,
  output [31:0] out_8,
  output [31:0] out_9,
  output [31:0] out_10,
  output [31:0] out_11,
  output [31:0] out_12,
  output [31:0] out_13,
  output [31:0] out_14,
  output [31:0] out_15,
  output [31:0] out_16,
  output [31:0] out_17,
  output [31:0] out_18,
  output [31:0] out_19,
  output [7:0] data_out,
  output [31:0] out_21,
  output [31:0] out_22,
  output [31:0] out_23,
  output [31:0] out_24,
  output [31:0] out_25,
  output [31:0] out_26,
  output [31:0] out_27,
  output [31:0] out_28,
  output [31:0] out_29,
  output [31:0] out_30,
  output [31:0] out_31,
  output [31:0] out_32,
  output [31:0] out_33,
  output [31:0] out_34,
  output [31:0] out_35,
  output [31:0] out_36,
  output [31:0] out_37,
  output [31:0] out_38
);

  wire and_1_out, and_2_out, and_3_out, decoder_1_out0, decoder_1_out1, decoder_1_out2, decoder_1_out3,
       decoder_1_out4, decoder_1_out5, decoder_1_out6, decoder_1_out7, decoder_1_out8, decoder_1_out9,
       decoder_1_out10, decoder_1_out11, decoder_1_out12, decoder_1_out13, decoder_1_out14, decoder_1_out15,
       decoder_1_out16, decoder_1_out17, decoder_1_out18, decoder_1_out19, decoder_1_out20, decoder_1_out21,
       decoder_1_out22, decoder_1_out23, decoder_1_out24, decoder_1_out25, decoder_1_out26, decoder_1_out27,
       decoder_1_out28, decoder_1_out29, decoder_1_out30, decoder_1_out31, video;
  wire [7:0] row0, row1, row2, row3, row4, row5, row6, row7, row8, row9, row10, row11, row12, row13, row14,
       row15, row16, row17, row18, row19, row20, row21, row22, row23, row24, row25, row26, row27, row28,
       row29, row30, row31, wrow0, wrow1, wrow2, wrow3, wrow4, wrow5, wrow6, wrow7, wrow8, wrow9, wrow10,
       wrow11, wrow12, wrow13, wrow14, wrow15, wrow16, wrow17, wrow18, wrow19, wrow20, wrow21, wrow22,
       wrow23, wrow24, wrow25, wrow26, wrow27, wrow28, wrow29, wrow30, wrow31;

  not not_1 (video, video_addr[5]);
  and and_1 (and_1_out, ~in_out, sel, video);  // AND_Gate
  Demultiplexer #(.select(5), .width(8), .disabled(0)) demultiplexer_1 (
    .out0(wrow0), .out1(wrow1), .out2(wrow2), .out3(wrow3), .out4(wrow4), .out5(wrow5), .out6(wrow6),
    .out7(wrow7), .out8(wrow8), .out9(wrow9), .out10(wrow10), .out11(wrow11), .out12(wrow12), .out13(wrow13),
    .out14(wrow14), .out15(wrow15), .out16(wrow16), .out17(wrow17), .out18(wrow18), .out19(wrow19),
    .out20(wrow20), .out21(wrow21), .out22(wrow22), .out23(wrow23), .out24(wrow24), .out25(wrow25),
    .out26(wrow26), .out27(wrow27), .out28(wrow28), .out29(wrow29), .out30(wrow30), .out31(wrow31),
    .in(data), .sel(video_addr[4:0]), .en(and_1_out));
  Multiplexer #(.select(5), .width(8)) multiplexer_1 (
    .in0(row0), .in1(row1), .in2(row2), .in3(row3), .in4(row4), .in5(row5), .in6(row6), .in7(row7),
    .in8(row8), .in9(row9), .in10(row10), .in11(row11), .in12(row12), .in13(row13), .in14(row14),
    .in15(row15), .in16(row16), .in17(row17), .in18(row18), .in19(row19), .in20(row20), .in21(row21),
    .in22(row22), .in23(row23), .in24(row24), .in25(row25), .in26(row26), .in27(row27), .in28(row28),
    .in29(row29), .in30(row30), .in31(row31), .out(data_out), .sel(video_addr[4:0]), .en(and_2_out));
  and and_2 (and_2_out, in_out, video, sel);
  and and_3 (and_3_out, ~in_out, sel, video);  // AND_Gate
  Decoder #(.select(5), .disabled(0)) decoder_1 (
    .out0(decoder_1_out0), .out1(decoder_1_out1), .out2(decoder_1_out2), .out3(decoder_1_out3),
    .out4(decoder_1_out4), .out5(decoder_1_out5), .out6(decoder_1_out6), .out7(decoder_1_out7),
    .out8(decoder_1_out8), .out9(decoder_1_out9), .out10(decoder_1_out10), .out11(decoder_1_out11),
    .out12(decoder_1_out12), .out13(decoder_1_out13), .out14(decoder_1_out14), .out15(decoder_1_out15),
    .out16(decoder_1_out16), .out17(decoder_1_out17), .out18(decoder_1_out18), .out19(decoder_1_out19),
    .out20(decoder_1_out20), .out21(decoder_1_out21), .out22(decoder_1_out22), .out23(decoder_1_out23),
    .out24(decoder_1_out24), .out25(decoder_1_out25), .out26(decoder_1_out26), .out27(decoder_1_out27),
    .out28(decoder_1_out28), .out29(decoder_1_out29), .out30(decoder_1_out30), .out31(decoder_1_out31),
    .sel(video_addr[4:0]), .en(and_3_out));
  Register #(.trigger("falling")) register_1 (.D(wrow15), .en(decoder_1_out15), .Q(row15), .clk(clock));  // open: clr
  Register #(.trigger("falling")) register_2 (.D(wrow14), .en(decoder_1_out14), .Q(row14), .clk(clock));  // open: clr
  Register #(.trigger("falling")) register_3 (.D(wrow13), .en(decoder_1_out13), .Q(row13), .clk(clock));  // open: clr
  Register #(.trigger("falling")) register_4 (.D(wrow12), .en(decoder_1_out12), .Q(row12), .clk(clock));  // open: clr
  Register #(.trigger("falling")) register_5 (.D(wrow11), .en(decoder_1_out11), .Q(row11), .clk(clock));  // open: clr
  Register #(.trigger("falling")) register_6 (.D(wrow10), .en(decoder_1_out10), .Q(row10), .clk(clock));  // open: clr
  Register #(.trigger("falling")) register_7 (.D(wrow9), .en(decoder_1_out9), .Q(row9), .clk(clock));  // open: clr
  Register #(.trigger("falling")) register_8 (.D(wrow8), .en(decoder_1_out8), .Q(row8), .clk(clock));  // open: clr
  Register #(.trigger("falling")) register_9 (.D(wrow7), .en(decoder_1_out7), .Q(row7), .clk(clock));  // open: clr
  Register #(.trigger("falling")) register_10 (.D(wrow6), .en(decoder_1_out6), .Q(row6), .clk(clock));  // open: clr
  Register #(.trigger("falling")) register_11 (.D(wrow5), .en(decoder_1_out5), .Q(row5), .clk(clock));  // open: clr
  Register #(.trigger("falling")) register_12 (.D(wrow4), .en(decoder_1_out4), .Q(row4), .clk(clock));  // open: clr
  Register #(.trigger("falling")) register_13 (.D(wrow3), .en(decoder_1_out3), .Q(row3), .clk(clock));  // open: clr
  Register #(.trigger("falling")) register_14 (.D(wrow2), .en(decoder_1_out2), .Q(row2), .clk(clock));  // open: clr
  Register #(.trigger("falling")) register_15 (.D(wrow1), .en(decoder_1_out1), .Q(row1), .clk(clock));  // open: clr
  Register #(.trigger("falling")) register_16 (.D(wrow0), .en(decoder_1_out0), .Q(row0), .clk(clock));  // open: clr
  Register #(.trigger("falling")) register_17 (.D(wrow16), .en(decoder_1_out16), .Q(row16), .clk(clock));  // open: clr
  Register #(.trigger("falling")) register_18 (.D(wrow17), .en(decoder_1_out17), .Q(row17), .clk(clock));  // open: clr
  Register #(.trigger("falling")) register_19 (.D(wrow18), .en(decoder_1_out18), .Q(row18), .clk(clock));  // open: clr
  Register #(.trigger("falling")) register_20 (.D(wrow19), .en(decoder_1_out19), .Q(row19), .clk(clock));  // open: clr
  Register #(.trigger("falling")) register_21 (.D(wrow20), .en(decoder_1_out20), .Q(row20), .clk(clock));  // open: clr
  Register #(.trigger("falling")) register_22 (.D(wrow21), .en(decoder_1_out21), .Q(row21), .clk(clock));  // open: clr
  Register #(.trigger("falling")) register_23 (.D(wrow22), .en(decoder_1_out22), .Q(row22), .clk(clock));  // open: clr
  Register #(.trigger("falling")) register_24 (.D(wrow23), .en(decoder_1_out23), .Q(row23), .clk(clock));  // open: clr
  Register #(.trigger("falling")) register_25 (.D(wrow24), .en(decoder_1_out24), .Q(row24), .clk(clock));  // open: clr
  Register #(.trigger("falling")) register_26 (.D(wrow25), .en(decoder_1_out25), .Q(row25), .clk(clock));  // open: clr
  Register #(.trigger("falling")) register_27 (.D(wrow26), .en(decoder_1_out26), .Q(row26), .clk(clock));  // open: clr
  Register #(.trigger("falling")) register_28 (.D(wrow27), .en(decoder_1_out27), .Q(row27), .clk(clock));  // open: clr
  Register #(.trigger("falling")) register_29 (.D(wrow28), .en(decoder_1_out28), .Q(row28), .clk(clock));  // open: clr
  Register #(.trigger("falling")) register_30 (.D(wrow29), .en(decoder_1_out29), .Q(row29), .clk(clock));  // open: clr
  Register #(.trigger("falling")) register_31 (.D(wrow30), .en(decoder_1_out30), .Q(row30), .clk(clock));  // open: clr
  Register #(.trigger("falling")) register_32 (.D(wrow31), .en(decoder_1_out31), .Q(row31), .clk(clock));  // open: clr
  dec dec_1 (.in_1(row31), .out_2(out_6));
  dec dec_2 (.in_1(row30), .out_2(out_7));
  dec dec_3 (.in_1(row29), .out_2(out_8));
  dec dec_4 (.in_1(row28), .out_2(out_9));
  dec dec_5 (.in_1(row27), .out_2(out_10));
  dec dec_6 (.in_1(row26), .out_2(out_11));
  dec dec_7 (.in_1(row25), .out_2(out_12));
  dec dec_8 (.in_1(row24), .out_2(out_13));
  dec dec_9 (.in_1(row23), .out_2(out_14));
  dec dec_10 (.in_1(row22), .out_2(out_15));
  dec dec_11 (.in_1(row21), .out_2(out_16));
  dec dec_12 (.in_1(row20), .out_2(out_17));
  dec dec_13 (.in_1(row19), .out_2(out_18));
  dec dec_14 (.in_1(row18), .out_2(out_19));
  dec dec_15 (.in_1(row17), .out_2(out_21));
  dec dec_16 (.in_1(row16), .out_2(out_22));
  dec dec_17 (.in_1(row15), .out_2(out_23));
  dec dec_18 (.in_1(row14), .out_2(out_24));
  dec dec_19 (.in_1(row13), .out_2(out_25));
  dec dec_20 (.in_1(row12), .out_2(out_26));
  dec dec_21 (.in_1(row11), .out_2(out_27));
  dec dec_22 (.in_1(row10), .out_2(out_28));
  dec dec_23 (.in_1(row9), .out_2(out_29));
  dec dec_24 (.in_1(row8), .out_2(out_30));
  dec dec_25 (.in_1(row7), .out_2(out_31));
  dec dec_26 (.in_1(row6), .out_2(out_32));
  dec dec_27 (.in_1(row5), .out_2(out_33));
  dec dec_28 (.in_1(row4), .out_2(out_34));
  dec dec_29 (.in_1(row3), .out_2(out_35));
  dec dec_30 (.in_1(row2), .out_2(out_36));
  dec dec_31 (.in_1(row1), .out_2(out_37));
  dec dec_32 (.in_1(row0), .out_2(out_38));

  // Other names for the same wires on the sheet: row_add[4:0] = video_addr[4:0]
endmodule

module Joystick (
  input  I_Osel,
  input  IN_OUT,
  input  Cl,
  input  [5:0] I_Oaddr,
  input  [1:0] Joystik_in,
  output [7:0] data_out
);

  wire and_1_out, and_2_out;
  wire [7:0] multiplexer_1_out;

  and and_1 (and_1_out, ~Joystik_in[0], Joystik_in[1]);  // AND_Gate
  and and_2 (and_2_out, Cl, IN_OUT, I_Osel, ~I_Oaddr[0], ~I_Oaddr[1], ~I_Oaddr[2], ~I_Oaddr[3], ~I_Oaddr[4], I_Oaddr[5]);  // AND_Gate
  Multiplexer #(.width(8), .enable("false")) multiplexer_1 (
    .in0({{7{1'b0}}, Joystik_in[1]}), .in1(8'h80), .out(multiplexer_1_out), .sel(and_1_out));
  assign data_out = and_2_out ? multiplexer_1_out : 8'bz;  // Controlled_Buffer controlled_buffer_1

  // Other names for the same wires on the sheet: Joystick_int[1:0] = Joystik_in
endmodule

module dec (
  input  [7:0] in_1,
  output [31:0] out_2
);

  wire and_1_out, decoder_2_out31, decoder_3_out30, decoder_3_out31;
  wire [31:0] decoder_1_out0;
  wire [31:1] decoder_2_out0;
  wire [31:2] decoder_3_out0;

  and and_1 (and_1_out, in_1[6], in_1[5]);
  Decoder #(.select(5), .disabled(0)) decoder_1 (
    .out0(decoder_1_out0[0]), .out1(decoder_1_out0[1]), .out2(decoder_1_out0[2]), .out3(decoder_1_out0[3]),
    .out4(decoder_1_out0[4]), .out5(decoder_1_out0[5]), .out6(decoder_1_out0[6]), .out7(decoder_1_out0[7]),
    .out8(decoder_1_out0[8]), .out9(decoder_1_out0[9]), .out10(decoder_1_out0[10]),
    .out11(decoder_1_out0[11]), .out12(decoder_1_out0[12]), .out13(decoder_1_out0[13]),
    .out14(decoder_1_out0[14]), .out15(decoder_1_out0[15]), .out16(decoder_1_out0[16]),
    .out17(decoder_1_out0[17]), .out18(decoder_1_out0[18]), .out19(decoder_1_out0[19]),
    .out20(decoder_1_out0[20]), .out21(decoder_1_out0[21]), .out22(decoder_1_out0[22]),
    .out23(decoder_1_out0[23]), .out24(decoder_1_out0[24]), .out25(decoder_1_out0[25]),
    .out26(decoder_1_out0[26]), .out27(decoder_1_out0[27]), .out28(decoder_1_out0[28]),
    .out29(decoder_1_out0[29]), .out30(decoder_1_out0[30]), .out31(decoder_1_out0[31]), .sel(in_1[4:0]),
    .en(in_1[5]));
  Decoder #(.select(5), .disabled(0)) decoder_2 (
    .out0(decoder_2_out0[1]), .out1(decoder_2_out0[2]), .out2(decoder_2_out0[3]), .out3(decoder_2_out0[4]),
    .out4(decoder_2_out0[5]), .out5(decoder_2_out0[6]), .out6(decoder_2_out0[7]), .out7(decoder_2_out0[8]),
    .out8(decoder_2_out0[9]), .out9(decoder_2_out0[10]), .out10(decoder_2_out0[11]),
    .out11(decoder_2_out0[12]), .out12(decoder_2_out0[13]), .out13(decoder_2_out0[14]),
    .out14(decoder_2_out0[15]), .out15(decoder_2_out0[16]), .out16(decoder_2_out0[17]),
    .out17(decoder_2_out0[18]), .out18(decoder_2_out0[19]), .out19(decoder_2_out0[20]),
    .out20(decoder_2_out0[21]), .out21(decoder_2_out0[22]), .out22(decoder_2_out0[23]),
    .out23(decoder_2_out0[24]), .out24(decoder_2_out0[25]), .out25(decoder_2_out0[26]),
    .out26(decoder_2_out0[27]), .out27(decoder_2_out0[28]), .out28(decoder_2_out0[29]),
    .out29(decoder_2_out0[30]), .out30(decoder_2_out0[31]), .out31(decoder_2_out31), .sel(in_1[4:0]),
    .en(and_1_out));
  Decoder #(.select(5), .disabled(0)) decoder_3 (
    .out0(decoder_3_out0[2]), .out1(decoder_3_out0[3]), .out2(decoder_3_out0[4]), .out3(decoder_3_out0[5]),
    .out4(decoder_3_out0[6]), .out5(decoder_3_out0[7]), .out6(decoder_3_out0[8]), .out7(decoder_3_out0[9]),
    .out8(decoder_3_out0[10]), .out9(decoder_3_out0[11]), .out10(decoder_3_out0[12]),
    .out11(decoder_3_out0[13]), .out12(decoder_3_out0[14]), .out13(decoder_3_out0[15]),
    .out14(decoder_3_out0[16]), .out15(decoder_3_out0[17]), .out16(decoder_3_out0[18]),
    .out17(decoder_3_out0[19]), .out18(decoder_3_out0[20]), .out19(decoder_3_out0[21]),
    .out20(decoder_3_out0[22]), .out21(decoder_3_out0[23]), .out22(decoder_3_out0[24]),
    .out23(decoder_3_out0[25]), .out24(decoder_3_out0[26]), .out25(decoder_3_out0[27]),
    .out26(decoder_3_out0[28]), .out27(decoder_3_out0[29]), .out28(decoder_3_out0[30]),
    .out29(decoder_3_out0[31]), .out30(decoder_3_out30), .out31(decoder_3_out31), .sel(in_1[4:0]),
    .en(and_1_out));
  assign out_2 = decoder_1_out0 | {decoder_2_out0, decoder_2_out0[1]} | {decoder_3_out0, {2{decoder_3_out0[2]}}};  // OR_Gate or_1, 32 bits wide

  // Other names for the same wires on the sheet: Coord[4:0] = in_1[4:0]; isWrite = in_1[5]; isColumn = in_1[6]
endmodule

module score_left (
  input  I_Osel,
  input  IN_OUT,
  input  Cl,
  input  [5:0] I_Oaddr,
  input  [7:0] data,
  output [7:0] value,
  output [7:0] data_out
);

  wire isRead, isWorking, isWrite;
  wire [7:0] register_1_q;

  and and_1 (isWorking, I_Oaddr[0], ~I_Oaddr[1], ~I_Oaddr[2], ~I_Oaddr[3], ~I_Oaddr[4], I_Oaddr[5]);  // AND_Gate
  and and_2 (isRead, I_Osel, isWorking, IN_OUT);
  and and_3 (isWrite, I_Osel, isWorking, ~IN_OUT);  // AND_Gate
  Register #(.trigger("falling")) register_1 (.D(data), .en(isWrite), .Q(register_1_q), .clk(Cl));  // open: clr
  assign data_out = isRead ? register_1_q : 8'bz;  // Controlled_Buffer controlled_buffer_1
  score_convertor score_convertor_1 (.in_1(register_1_q), .out_2(value));

  // Other names for the same wires on the sheet: clock = Cl; sel = I_Osel
endmodule

module score_convertor (
  input  [7:0] in_1,
  output [7:0] out_2
);

  wire comparator_1_eq, comparator_1_gt, comparator_1_lt, comparator_2_eq, comparator_2_gt, comparator_2_lt;
  wire [3:0] adder_1_out, adder_2_out, adder_3_out, multiplexer_2_out;

  Adder #(.width(4)) adder_1 (.a(4'b0110), .b(in_1[3:0]), .out(adder_1_out));  // open: cin, cout
  Comparator #(.width(4), .mode("unsigned")) comparator_1 (
    .a(in_1[3:0]), .b(4'b1001), .gt(comparator_1_gt), .eq(comparator_1_eq), .lt(comparator_1_lt));
  Adder #(.width(4)) adder_2 (.a(in_1[7:4]), .b(4'b0001), .out(adder_2_out));  // open: cin, cout
  Multiplexer #(.width(4), .enable("false")) multiplexer_1 (
    .in0(in_1[3:0]), .in1(adder_1_out), .out(out_2[3:0]), .sel(comparator_1_gt));
  Multiplexer #(.width(4), .enable("false")) multiplexer_2 (
    .in0(in_1[7:4]), .in1(adder_2_out), .out(multiplexer_2_out), .sel(comparator_1_gt));
  Adder #(.width(4)) adder_3 (.a(4'b0110), .b(multiplexer_2_out), .out(adder_3_out));  // open: cin, cout
  Comparator #(.width(4), .mode("unsigned")) comparator_2 (
    .a(multiplexer_2_out), .b(4'b1001), .gt(comparator_2_gt), .eq(comparator_2_eq), .lt(comparator_2_lt));
  Multiplexer #(.width(4), .enable("false")) multiplexer_3 (
    .in0(multiplexer_2_out), .in1(adder_3_out), .out(out_2[7:4]), .sel(comparator_2_gt));
endmodule

module score_right (
  input  I_Osel,
  input  IN_OUT,
  input  Cl,
  input  [5:0] I_Oaddr,
  input  [7:0] data,
  output [7:0] value,
  output [7:0] data_out
);

  wire isRead, isWorking, isWrite;
  wire [7:0] register_1_q;

  and and_1 (isWorking, ~I_Oaddr[0], I_Oaddr[1], ~I_Oaddr[2], ~I_Oaddr[3], ~I_Oaddr[4], I_Oaddr[5]);  // AND_Gate
  and and_2 (isRead, I_Osel, isWorking, IN_OUT);
  and and_3 (isWrite, I_Osel, isWorking, ~IN_OUT);  // AND_Gate
  Register #(.trigger("falling")) register_1 (.D(data), .en(isWrite), .Q(register_1_q), .clk(Cl));  // open: clr
  assign data_out = isRead ? register_1_q : 8'bz;  // Controlled_Buffer controlled_buffer_1
  score_convertor score_convertor_1 (.in_1(register_1_q), .out_2(value));

  // Other names for the same wires on the sheet: clock = Cl; sel = I_Osel
endmodule

module Update (
  input  I_Osel,
  input  IN_OUT,
  input  Cl,
  input  [5:0] I_Oaddr,
  input  [7:0] data,
  output [7:0] data_out
);

  wire adder_2_cout, and_16_out, and_17_out, comparator_1_eq, comparator_1_gt, comparator_1_lt,
       comparator_2_gt, comparator_3_lt, isRead_upd, isRead_V, isRead_xBall, isRead_yBall,
       isWorking_reflectX, isWorking_reflectY, isWorking_upd, isWorking_V, isWorking_xBall, isWorking_yBall,
       isWrite_reflectX, isWrite_reflectY, isWrite_V, isWrite_xBall, isWrite_yBall, or_1_out, or_2_out,
       or_3_out, or_4_out;
  wire [3:0] not_1_out, not_2_out, V_reflectX;
  wire [7:0] adder_1_out, adder_2_out, controlled_buffer_1_out, controlled_buffer_4_out,
       controlled_buffer_6_out, dx, dy, multiplexer_1_out, multiplexer_3_out, newX, newY, x, y;
  wire [7:4] V_reflectY;

  and and_1 (isRead_upd, I_Osel, isWorking_upd, IN_OUT);
  and and_2 (isRead_xBall, I_Osel, isWorking_xBall, IN_OUT);
  and and_3 (isWrite_xBall, I_Osel, isWorking_xBall, ~IN_OUT);  // AND_Gate
  and and_4 (isRead_yBall, I_Osel, isWorking_yBall, IN_OUT);
  and and_5 (isWrite_yBall, I_Osel, isWorking_yBall, ~IN_OUT);  // AND_Gate
  and and_6 (isWrite_reflectX, I_Osel, isWorking_reflectX, ~IN_OUT);  // AND_Gate
  and and_7 (isWrite_reflectY, I_Osel, isWorking_reflectY, ~IN_OUT);  // AND_Gate
  and and_8 (isWorking_yBall, I_Oaddr[0], ~I_Oaddr[1], I_Oaddr[2], ~I_Oaddr[3], ~I_Oaddr[4], I_Oaddr[5]);  // AND_Gate
  and and_9 (isWorking_xBall, ~I_Oaddr[0], ~I_Oaddr[1], I_Oaddr[2], ~I_Oaddr[3], ~I_Oaddr[4], I_Oaddr[5]);  // AND_Gate
  and and_10 (isWorking_upd, ~I_Oaddr[0], I_Oaddr[1], I_Oaddr[2], ~I_Oaddr[3], ~I_Oaddr[4], I_Oaddr[5]);  // AND_Gate
  and and_11 (isWorking_V, I_Oaddr[0], I_Oaddr[1], ~I_Oaddr[2], ~I_Oaddr[3], ~I_Oaddr[4], I_Oaddr[5]);  // AND_Gate
  and and_12 (isWorking_reflectX, I_Oaddr[0], I_Oaddr[1], I_Oaddr[2], ~I_Oaddr[3], ~I_Oaddr[4], I_Oaddr[5]);  // AND_Gate
  and and_13 (isWorking_reflectY, ~I_Oaddr[0], ~I_Oaddr[1], ~I_Oaddr[2], I_Oaddr[3], ~I_Oaddr[4], I_Oaddr[5]);  // AND_Gate
  and and_14 (isRead_V, I_Osel, isWorking_V, IN_OUT);
  and and_15 (isWrite_V, I_Osel, isWorking_V, ~IN_OUT);  // AND_Gate
  assign controlled_buffer_1_out = isWrite_reflectX ? {dy[7], dy[3:1], V_reflectX} : 8'bz;  // Controlled_Buffer controlled_buffer_1
  assign controlled_buffer_1_out = isWrite_reflectY ? {V_reflectY, dx[7], dx[3:1]} : 8'bz;  // Controlled_Buffer controlled_buffer_2
  assign controlled_buffer_1_out = isWrite_V ? data : 8'bz;  // Controlled_Buffer controlled_buffer_3
  or or_1 (or_1_out, isWrite_reflectX, isWrite_V, isWrite_reflectY);
  assign controlled_buffer_4_out = isRead_upd ? newX : 8'bz;  // Controlled_Buffer controlled_buffer_4
  assign controlled_buffer_4_out = isWrite_xBall ? data : 8'bz;  // Controlled_Buffer controlled_buffer_5
  assign controlled_buffer_6_out = isRead_upd ? newY : 8'bz;  // Controlled_Buffer controlled_buffer_6
  assign controlled_buffer_6_out = isWrite_yBall ? data : 8'bz;  // Controlled_Buffer controlled_buffer_7
  or or_2 (or_2_out, isRead_upd, isWrite_xBall);
  Register #(.trigger("falling")) register_1 (
    .D(controlled_buffer_1_out), .en(or_1_out), .Q({dy[7], dy[3:1], dx[7], dx[3:1]}), .clk(Cl));  // open: clr
  Register #(.trigger("falling")) register_2 (
    .D(controlled_buffer_4_out), .en(or_2_out), .Q({x[2:0], x[7:3]}), .clk(Cl));  // open: clr
  Register #(.trigger("falling")) register_3 (
    .D(controlled_buffer_6_out), .en(or_3_out), .Q({y[2:0], y[7:3]}), .clk(Cl));  // open: clr
  or or_3 (or_3_out, isRead_upd, isWrite_yBall);
  Comparator #(.mode("unsigned")) comparator_1 (
    .a(adder_2_out), .b(y), .gt(comparator_1_gt), .eq(comparator_1_eq), .lt(comparator_1_lt));
  or or_4 (or_4_out, comparator_1_gt, comparator_1_eq);
  assign data_out = isRead_V ? {dy[7], dy[3:1], dx[7], dx[3:1]} : 8'bz;  // Controlled_Buffer controlled_buffer_8
  Adder adder_1 (.a(x), .b({{4{dx[7]}}, dx[3:0]}), .out(adder_1_out));  // open: cin, cout
  Comparator #(.mode("unsigned")) comparator_2 (.a(8'h9), .b(x), .gt(comparator_2_gt));  // open: eq, lt
  Comparator #(.mode("unsigned")) comparator_3 (.a(8'hf0), .b(x), .lt(comparator_3_lt));  // open: gt, eq
  Adder adder_2 (.a(y), .b({{4{dy[7]}}, dy[3:0]}), .out(adder_2_out), .cout(adder_2_cout));  // open: cin
  assign not_1_out = ~{dx[7], dx[3:1]};  // NOT_Gate not_1, 4 bits wide
  assign not_2_out = ~{dy[7], dy[3:1]};  // NOT_Gate not_2, 4 bits wide
  assign data_out = isRead_xBall ? {3'b000, x[7:3]} : 8'bz;  // Controlled_Buffer controlled_buffer_9
  assign data_out = isRead_yBall ? {3'b000, y[7:3]} : 8'bz;  // Controlled_Buffer controlled_buffer_10
  assign data_out = isRead_upd ? {3'b000, x[7:3]} : 8'bz;  // Controlled_Buffer controlled_buffer_11
  and and_16 (and_16_out, ~dy[7], adder_2_cout, comparator_1_lt);  // AND_Gate
  and and_17 (and_17_out, dy[7], or_4_out);
  Adder #(.width(4)) adder_3 (.a(4'b0001), .b(not_1_out), .out(V_reflectX));  // open: cin, cout
  Adder #(.width(4)) adder_4 (.a(4'b0001), .b(not_2_out), .out(V_reflectY));  // open: cin, cout
  not not_3 (dx[0], dx[7]);
  Multiplexer #(.width(8), .enable("false")) multiplexer_1 (
    .in0({adder_1_out[2:0], adder_1_out[7:3]}), .in1(8'h2), .out(multiplexer_1_out), .sel(comparator_2_gt));
  Multiplexer #(.width(8), .enable("false")) multiplexer_2 (
    .in0(multiplexer_1_out), .in1(8'h1d), .out(newX), .sel(comparator_3_lt));
  not not_4 (dy[0], dy[7]);
  Multiplexer #(.width(8), .enable("false")) multiplexer_3 (
    .in0({adder_2_out[2:0], adder_2_out[7:3]}), .in1(8'h1f), .out(multiplexer_3_out), .sel(and_16_out));
  Multiplexer #(.width(8), .enable("false")) multiplexer_4 (
    .in0(multiplexer_3_out), .in1({8{1'b0}}), .out(newY), .sel(and_17_out));

  // Other names for the same wires on the sheet: addr[5:0] = I_Oaddr; V[7:0] = {dy[7], dy[3:1], dx[7], dx[3:1]};
  //   V_reflectY[3:0] = {dx[7], dx[3:1]}; dx[6:4] = {3{dx[7]}}; V_reflectX[7:4] = {dy[7], dy[3:1]};
  //   dy[6:4] = {3{dy[7]}}; sel = I_Osel
endmodule

module TV_TENNIS (
  input  Cl,
  input  I_Osel,
  input  [7:0] I_Odata,
  input  IN_OUT,
  input  [7:0] score_right,
  input  [5:0] I_Oaddr,
  input  [7:0] score_left,
  output [1:0] Joystick,
  output [7:0] data_out
);

  wire [31:0] video_buffer_1_out_6, video_buffer_1_out_7, video_buffer_1_out_8, video_buffer_1_out_9,
       video_buffer_1_out_10, video_buffer_1_out_11, video_buffer_1_out_12, video_buffer_1_out_13,
       video_buffer_1_out_14, video_buffer_1_out_15, video_buffer_1_out_16, video_buffer_1_out_17,
       video_buffer_1_out_18, video_buffer_1_out_19, video_buffer_1_out_21, video_buffer_1_out_22,
       video_buffer_1_out_23, video_buffer_1_out_24, video_buffer_1_out_25, video_buffer_1_out_26,
       video_buffer_1_out_27, video_buffer_1_out_28, video_buffer_1_out_29, video_buffer_1_out_30,
       video_buffer_1_out_31, video_buffer_1_out_32, video_buffer_1_out_33, video_buffer_1_out_34,
       video_buffer_1_out_35, video_buffer_1_out_36, video_buffer_1_out_37, video_buffer_1_out_38;

  Hex_Digit_Display hex_digit_display_1 (.value(score_left[7:4]));  // open: dp
  Joystick_part #(.bits(2)) joystick_1 (.y(Joystick));  // open: x
  Hex_Digit_Display hex_digit_display_2 (.value(score_left[3:0]));  // open: dp
  DotMatrix #(.matrixcols(32), .matrixrows(32)) dotmatrix_1 (
    .col0(video_buffer_1_out_38), .col1(video_buffer_1_out_37), .col2(video_buffer_1_out_36),
    .col3(video_buffer_1_out_35), .col4(video_buffer_1_out_34), .col5(video_buffer_1_out_33),
    .col6(video_buffer_1_out_32), .col7(video_buffer_1_out_31), .col8(video_buffer_1_out_30),
    .col9(video_buffer_1_out_29), .col10(video_buffer_1_out_28), .col11(video_buffer_1_out_27),
    .col12(video_buffer_1_out_26), .col13(video_buffer_1_out_25), .col14(video_buffer_1_out_24),
    .col15(video_buffer_1_out_23), .col16(video_buffer_1_out_22), .col17(video_buffer_1_out_21),
    .col18(video_buffer_1_out_19), .col19(video_buffer_1_out_18), .col20(video_buffer_1_out_17),
    .col21(video_buffer_1_out_16), .col22(video_buffer_1_out_15), .col23(video_buffer_1_out_14),
    .col24(video_buffer_1_out_13), .col25(video_buffer_1_out_12), .col26(video_buffer_1_out_11),
    .col27(video_buffer_1_out_10), .col28(video_buffer_1_out_9), .col29(video_buffer_1_out_8),
    .col30(video_buffer_1_out_7), .col31(video_buffer_1_out_6));
  video_buffer video_buffer_1 (
    .video_addr(I_Oaddr), .sel(I_Osel), .in_out(IN_OUT), .clock(Cl), .data(I_Odata), .data_out(data_out),
    .out_6(video_buffer_1_out_6), .out_7(video_buffer_1_out_7), .out_8(video_buffer_1_out_8),
    .out_9(video_buffer_1_out_9), .out_10(video_buffer_1_out_10), .out_11(video_buffer_1_out_11),
    .out_12(video_buffer_1_out_12), .out_13(video_buffer_1_out_13), .out_14(video_buffer_1_out_14),
    .out_15(video_buffer_1_out_15), .out_16(video_buffer_1_out_16), .out_17(video_buffer_1_out_17),
    .out_18(video_buffer_1_out_18), .out_19(video_buffer_1_out_19), .out_21(video_buffer_1_out_21),
    .out_22(video_buffer_1_out_22), .out_23(video_buffer_1_out_23), .out_24(video_buffer_1_out_24),
    .out_25(video_buffer_1_out_25), .out_26(video_buffer_1_out_26), .out_27(video_buffer_1_out_27),
    .out_28(video_buffer_1_out_28), .out_29(video_buffer_1_out_29), .out_30(video_buffer_1_out_30),
    .out_31(video_buffer_1_out_31), .out_32(video_buffer_1_out_32), .out_33(video_buffer_1_out_33),
    .out_34(video_buffer_1_out_34), .out_35(video_buffer_1_out_35), .out_36(video_buffer_1_out_36),
    .out_37(video_buffer_1_out_37), .out_38(video_buffer_1_out_38));
  Hex_Digit_Display hex_digit_display_3 (.value(score_right[7:4]));  // open: dp
  Hex_Digit_Display hex_digit_display_4 (.value(score_right[3:0]));  // open: dp
endmodule

module Random (
  input  I_Osel,
  input  IN_OUT,
  input  Cl,
  input  [5:0] I_Oaddr,
  output [7:0] data_out
);

  wire isRead, isWorking, undriven;
  wire [7:0] random_1_out;

  and and_1 (isRead, isWorking, I_Osel, IN_OUT);
  and and_2 (isWorking, I_Oaddr[0], ~I_Oaddr[1], ~I_Oaddr[2], I_Oaddr[3], ~I_Oaddr[4], I_Oaddr[5]);  // AND_Gate
  Random_part #(.trigger("falling")) random_1 (.clk(Cl), .next(isRead), .out(random_1_out), .clr(undriven));
  assign data_out = isRead ? random_1_out : 8'bz;  // Controlled_Buffer controlled_buffer_1

  // Other names for the same wires on the sheet: sel = I_Osel
endmodule
